// Logisim project 16-BitSingleCycleProcessor-AbdullahCosgun-AycanDenizVit.circ as structural Verilog: 1 circuit, main circuit 16-bit Single Cycle Processor
module _16_bit_Single_Cycle_Processor (
  output [15:0] out_1,
  output [15:0] out_2,
  output [15:0] out_3,
  output [15:0] out_4,
  output [15:0] out_5,
  output [31:0] out_6
);

  wire alu_1_out_6, and_1_out, clock_2_out, clock_out, control_unit_1_adds, control_unit_1_alusrc,
       control_unit_1_branch, control_unit_1_jump, control_unit_1_memread, control_unit_1_memtoreg,
       control_unit_1_memwrite, control_unit_1_regdst, control_unit_1_regwrite, reset_2_out, reset_3_out,
       reset_out;
  wire [3:0] instruction_fetch_1_op, instruction_fetch_1_rd, instruction_fetch_1_rs, instruction_fetch_1_rt,
       instruction_fetch_1_shamt, multiplexer_2_out;
  wire [15:0] adder_2_output, instruction_fetch_1_i_immediate, instruction_fetch_1_j_target_address,
       multiplexer_1_out, multiplexer_3_out, multiplexer_4_out, multiplexer_5_out, multiplexer_6_out,
       ram_1_data, register_1_q;

  Register #(.width(16)) register_1 (
    .D(multiplexer_1_out), .en(1'b1), .Q(register_1_q), .clk(clock_out), .clr(reset_out));
  Button reset (.out(reset_out));
  Clock clock (.out(clock_out));
  Multiplexer #(.width(16), .enable("false")) multiplexer_1 (
    .in0(multiplexer_4_out), .in1(instruction_fetch_1_j_target_address), .out(multiplexer_1_out),
    .sel(control_unit_1_jump));
  Adder adder_1 (.Data1(register_1_q), .Data2(16'h1), .Output(out_1));
  ROM #(.addrWidth(16), .dataWidth(32)) rom_1 (.addr(register_1_q), .data(out_6));  // open: sel
  Instruction_Fetch instruction_fetch_1 (
    .in_1(out_6), .rd(instruction_fetch_1_rd), .rt(instruction_fetch_1_rt), .rs(instruction_fetch_1_rs),
    .op(instruction_fetch_1_op), .I_immediate(instruction_fetch_1_i_immediate),
    .J_Target_Address(instruction_fetch_1_j_target_address), .shamt(instruction_fetch_1_shamt));
  Multiplexer #(.width(4), .enable("false")) multiplexer_2 (
    .in0(instruction_fetch_1_rt), .in1(instruction_fetch_1_rd), .out(multiplexer_2_out),
    .sel(control_unit_1_regdst));
  Button reset_2 (.out(reset_2_out));
  Control_Unit control_unit_1 (
    .in_1(instruction_fetch_1_op), .RegDst(control_unit_1_regdst), .ALUSrc(control_unit_1_alusrc),
    .MemToReg(control_unit_1_memtoreg), .RegWrite(control_unit_1_regwrite), .MemRead(control_unit_1_memread),
    .MemWrite(control_unit_1_memwrite), .Branch(control_unit_1_branch), .Jump(control_unit_1_jump),
    .ADDS(control_unit_1_adds));
  Register_File register_file_1 (
    .Write_Data(out_5), .rd(multiplexer_2_out), .reset(reset_2_out), .RegWrite(control_unit_1_regwrite),
    .rs(instruction_fetch_1_rs), .rt(instruction_fetch_1_rt), .data2__rt(out_2), .data1__rs(out_3));
  Adder adder_2 (.Data1(out_1), .Data2(instruction_fetch_1_i_immediate), .Output(adder_2_output));
  Multiplexer #(.width(16), .enable("false")) multiplexer_3 (
    .in0(out_2), .in1(instruction_fetch_1_i_immediate), .out(multiplexer_3_out), .sel(control_unit_1_alusrc));
  Multiplexer #(.width(16), .enable("false")) multiplexer_4 (
    .in0(out_1), .in1(adder_2_output), .out(multiplexer_4_out), .sel(and_1_out));
  and and_1 (and_1_out, control_unit_1_branch, alu_1_out_6);
  ALU alu_1 (
    .Data1(out_3), .Data2(multiplexer_3_out), .ALU_Control__from_opcode(instruction_fetch_1_op),
    .out_5(out_4), .out_6(alu_1_out_6), .Shamt(instruction_fetch_1_shamt));
  Multiplexer #(.width(16), .enable("false")) multiplexer_5 (
    .in0(out_4), .in1(out_2), .out(multiplexer_5_out), .sel(control_unit_1_adds));
  Multiplexer #(.width(16), .enable("false")) multiplexer_6 (
    .in0(out_2), .in1(out_4), .out(multiplexer_6_out), .sel(control_unit_1_adds));
  Clock clock_2 (.out(clock_2_out));
  RAM #(.addrWidth(16), .dataWidth(16), .bus("separate")) ram_1 (
    .addr(multiplexer_5_out), .din(multiplexer_6_out), .data(ram_1_data), .str(control_unit_1_memwrite),
    .clk(clock_2_out), .ld(control_unit_1_memread), .clr(reset_3_out));  // open: sel
  Button reset_3 (.out(reset_3_out));
  Multiplexer #(.width(16), .enable("false")) multiplexer_7 (
    .in0(out_4), .in1(ram_1_data), .out(out_5), .sel(control_unit_1_memtoreg));

  // Notes on the sheet:
  //   contents of rom_1 (hex, n*v repeats v):
  //   14010000 14050000 14060004 30a60005 253800 28e80000 3d003800 14a50001 38000003 14090001
endmodule
