// Logisim project project.circ as structural Verilog
// HA
module Half_Adder (
  input  Data1,
  input  Data2,
  output Sum,
  output CarryOut
);

  xor xor_1 (Sum, Data1, Data2);
  and and_1 (CarryOut, Data1, Data2);

  // Notes on the sheet:
  //   HALF ADDER
endmodule

// FA
module Full_Adder (
  input  Data1,
  input  Data2,
  input  Cin,
  output Sum,
  output Cout
);

  wire Half_Adder_2_carryout, Half_Adder_carryout, Half_Adder_sum;

  Half_Adder Half_Adder (.Data1(Data1), .Data2(Data2), .Sum(Half_Adder_sum), .CarryOut(Half_Adder_carryout));
  Half_Adder Half_Adder_2 (.Data1(Half_Adder_sum), .Data2(Cin), .Sum(Sum), .CarryOut(Half_Adder_2_carryout));
  or or_1 (Cout, Half_Adder_2_carryout, Half_Adder_carryout);

  // Notes on the sheet:
  //   Full Adder
endmodule

// Add
module Adder (
  input  [31:0] Data1,
  input  [31:0] Data2,
  output [31:0] Output,
  output Overflow
);

  wire full_adder_1_cout, full_adder_2_cout, full_adder_3_cout, full_adder_4_cout, full_adder_5_cout,
       full_adder_6_cout, full_adder_7_cout, full_adder_8_cout, full_adder_9_cout, full_adder_10_cout,
       full_adder_11_cout, full_adder_12_cout, full_adder_13_cout, full_adder_14_cout, full_adder_15_cout,
       full_adder_16_cout, full_adder_17_cout, full_adder_18_cout, full_adder_19_cout, full_adder_20_cout,
       full_adder_21_cout, full_adder_22_cout, full_adder_23_cout, full_adder_24_cout, full_adder_25_cout,
       full_adder_26_cout, full_adder_27_cout, full_adder_28_cout, full_adder_29_cout, full_adder_30_cout,
       full_adder_31_cout;

  Full_Adder full_adder_1 (.Data1(Data1[0]), .Data2(Data2[0]), .Cin(1'b0), .Sum(Output[0]), .Cout(full_adder_1_cout));
  Full_Adder full_adder_2 (
    .Data1(Data1[1]), .Data2(Data2[1]), .Cin(full_adder_1_cout), .Sum(Output[1]), .Cout(full_adder_2_cout));
  Full_Adder full_adder_3 (
    .Data1(Data1[2]), .Data2(Data2[2]), .Cin(full_adder_2_cout), .Sum(Output[2]), .Cout(full_adder_3_cout));
  Full_Adder full_adder_4 (
    .Data1(Data1[3]), .Data2(Data2[3]), .Cin(full_adder_3_cout), .Sum(Output[3]), .Cout(full_adder_4_cout));
  Full_Adder full_adder_5 (
    .Data1(Data1[4]), .Data2(Data2[4]), .Cin(full_adder_4_cout), .Sum(Output[4]), .Cout(full_adder_5_cout));
  Full_Adder full_adder_6 (
    .Data1(Data1[5]), .Data2(Data2[5]), .Cin(full_adder_5_cout), .Sum(Output[5]), .Cout(full_adder_6_cout));
  Full_Adder full_adder_7 (
    .Data1(Data1[6]), .Data2(Data2[6]), .Cin(full_adder_6_cout), .Sum(Output[6]), .Cout(full_adder_7_cout));
  Full_Adder full_adder_8 (
    .Data1(Data1[7]), .Data2(Data2[7]), .Cin(full_adder_7_cout), .Sum(Output[7]), .Cout(full_adder_8_cout));
  Full_Adder full_adder_9 (
    .Data1(Data1[8]), .Data2(Data2[8]), .Cin(full_adder_8_cout), .Sum(Output[8]), .Cout(full_adder_9_cout));
  Full_Adder full_adder_10 (
    .Data1(Data1[9]), .Data2(Data2[9]), .Cin(full_adder_9_cout), .Sum(Output[9]), .Cout(full_adder_10_cout));
  Full_Adder full_adder_11 (
    .Data1(Data1[10]), .Data2(Data2[10]), .Cin(full_adder_10_cout), .Sum(Output[10]),
    .Cout(full_adder_11_cout));
  Full_Adder full_adder_12 (
    .Data1(Data1[11]), .Data2(Data2[11]), .Cin(full_adder_11_cout), .Sum(Output[11]),
    .Cout(full_adder_12_cout));
  Full_Adder full_adder_13 (
    .Data1(Data1[12]), .Data2(Data2[12]), .Cin(full_adder_12_cout), .Sum(Output[12]),
    .Cout(full_adder_13_cout));
  Full_Adder full_adder_14 (
    .Data1(Data1[13]), .Data2(Data2[13]), .Cin(full_adder_13_cout), .Sum(Output[13]),
    .Cout(full_adder_14_cout));
  Full_Adder full_adder_15 (
    .Data1(Data1[14]), .Data2(Data2[14]), .Cin(full_adder_14_cout), .Sum(Output[14]),
    .Cout(full_adder_15_cout));
  Full_Adder full_adder_16 (
    .Data1(Data1[15]), .Data2(Data2[15]), .Cin(full_adder_15_cout), .Sum(Output[15]),
    .Cout(full_adder_16_cout));
  Full_Adder full_adder_17 (
    .Data1(Data1[16]), .Data2(Data2[16]), .Cin(full_adder_16_cout), .Sum(Output[16]),
    .Cout(full_adder_17_cout));
  Full_Adder full_adder_18 (
    .Data1(Data1[17]), .Data2(Data2[17]), .Cin(full_adder_17_cout), .Sum(Output[17]),
    .Cout(full_adder_18_cout));
  Full_Adder full_adder_19 (
    .Data1(Data1[18]), .Data2(Data2[18]), .Cin(full_adder_18_cout), .Sum(Output[18]),
    .Cout(full_adder_19_cout));
  Full_Adder full_adder_20 (
    .Data1(Data1[19]), .Data2(Data2[19]), .Cin(full_adder_19_cout), .Sum(Output[19]),
    .Cout(full_adder_20_cout));
  Full_Adder full_adder_21 (
    .Data1(Data1[20]), .Data2(Data2[20]), .Cin(full_adder_20_cout), .Sum(Output[20]),
    .Cout(full_adder_21_cout));
  Full_Adder full_adder_22 (
    .Data1(Data1[21]), .Data2(Data2[21]), .Cin(full_adder_21_cout), .Sum(Output[21]),
    .Cout(full_adder_22_cout));
  Full_Adder full_adder_23 (
    .Data1(Data1[22]), .Data2(Data2[22]), .Cin(full_adder_22_cout), .Sum(Output[22]),
    .Cout(full_adder_23_cout));
  Full_Adder full_adder_24 (
    .Data1(Data1[23]), .Data2(Data2[23]), .Cin(full_adder_23_cout), .Sum(Output[23]),
    .Cout(full_adder_24_cout));
  Full_Adder full_adder_25 (
    .Data1(Data1[24]), .Data2(Data2[24]), .Cin(full_adder_24_cout), .Sum(Output[24]),
    .Cout(full_adder_25_cout));
  Full_Adder full_adder_26 (
    .Data1(Data1[25]), .Data2(Data2[25]), .Cin(full_adder_25_cout), .Sum(Output[25]),
    .Cout(full_adder_26_cout));
  Full_Adder full_adder_27 (
    .Data1(Data1[26]), .Data2(Data2[26]), .Cin(full_adder_26_cout), .Sum(Output[26]),
    .Cout(full_adder_27_cout));
  Full_Adder full_adder_28 (
    .Data1(Data1[27]), .Data2(Data2[27]), .Cin(full_adder_27_cout), .Sum(Output[27]),
    .Cout(full_adder_28_cout));
  Full_Adder full_adder_29 (
    .Data1(Data1[28]), .Data2(Data2[28]), .Cin(full_adder_28_cout), .Sum(Output[28]),
    .Cout(full_adder_29_cout));
  Full_Adder full_adder_30 (
    .Data1(Data1[29]), .Data2(Data2[29]), .Cin(full_adder_29_cout), .Sum(Output[29]),
    .Cout(full_adder_30_cout));
  Full_Adder full_adder_31 (
    .Data1(Data1[30]), .Data2(Data2[30]), .Cin(full_adder_30_cout), .Sum(Output[30]),
    .Cout(full_adder_31_cout));
  Full_Adder full_adder_32 (
    .Data1(Data1[31]), .Data2(Data2[31]), .Cin(full_adder_31_cout), .Sum(Output[31]), .Cout(Overflow));
endmodule

module ALU (
  input  [15:0] Data1,
  input  [15:0] Data2,
  input  [2:0] ALU_Control,
  output [15:0] out_4
);

  wire comparator_1_lt;
  wire [15:0] and_1_out, bit_extender_1_out, multiplier_1_out, or_1_out, shifter_1_out, shifter_2_out,
       undriven, undriven_2;

  Register #(.width(16)) register_1 ();  // open: D, en, Q, clk, clr
  assign and_1_out = Data1 & Data2;  // AND_Gate and_1, 16 bits wide
  assign or_1_out = Data1 | Data2;  // OR_Gate or_1, 16 bits wide
  Shifter #(.width(16)) shifter_1 (.in(Data1), .\dist (Data2[3:0]), .out(shifter_1_out));
  Shifter #(.width(16), .shift("lr")) shifter_2 (.in(Data1), .\dist (Data2[3:0]), .out(shifter_2_out));
  Multiplier #(.width(16)) multiplier_1 (.a(Data1), .b(Data2), .out(multiplier_1_out));  // open: cin, cout
  Comparator #(.width(16)) comparator_1 (.a(Data1), .b(Data2), .lt(comparator_1_lt));  // open: gt, eq
  assign bit_extender_1_out = {{15{1'b0}}, comparator_1_lt};  // Bit_Extender bit_extender_1
  Multiplexer #(.select(3), .width(16), .enable("false")) multiplexer_1 (
    .in0(and_1_out), .in1(or_1_out), .in2(undriven), .in3(undriven_2), .in4(shifter_1_out),
    .in5(shifter_2_out), .in6(multiplier_1_out), .in7(bit_extender_1_out), .out(out_4), .sel(ALU_Control));
endmodule

// Sub
module Subtractor (
  input  [31:0] Data1,
  input  [31:0] Data2,
  output [31:0] Output,
  output Overflow
);

  wire full_adder_1_cout, full_adder_2_cout, full_adder_3_cout, full_adder_4_cout, full_adder_5_cout,
       full_adder_6_cout, full_adder_7_cout, full_adder_8_cout, full_adder_9_cout, full_adder_10_cout,
       full_adder_11_cout, full_adder_12_cout, full_adder_13_cout, full_adder_14_cout, full_adder_15_cout,
       full_adder_16_cout, full_adder_17_cout, full_adder_18_cout, full_adder_19_cout, full_adder_20_cout,
       full_adder_21_cout, full_adder_22_cout, full_adder_23_cout, full_adder_24_cout, full_adder_25_cout,
       full_adder_26_cout, full_adder_27_cout, full_adder_28_cout, full_adder_29_cout, full_adder_30_cout,
       full_adder_31_cout;
  wire [31:0] not_1_out;

  assign not_1_out = ~Data2;  // NOT_Gate not_1, 32 bits wide
  Full_Adder full_adder_1 (
    .Data1(Data1[0]), .Data2(not_1_out[0]), .Cin(1'b1), .Sum(Output[0]), .Cout(full_adder_1_cout));
  Full_Adder full_adder_2 (
    .Data1(Data1[1]), .Data2(not_1_out[1]), .Cin(full_adder_1_cout), .Sum(Output[1]), .Cout(full_adder_2_cout));
  Full_Adder full_adder_3 (
    .Data1(Data1[2]), .Data2(not_1_out[2]), .Cin(full_adder_2_cout), .Sum(Output[2]), .Cout(full_adder_3_cout));
  Full_Adder full_adder_4 (
    .Data1(Data1[3]), .Data2(not_1_out[3]), .Cin(full_adder_3_cout), .Sum(Output[3]), .Cout(full_adder_4_cout));
  Full_Adder full_adder_5 (
    .Data1(Data1[4]), .Data2(not_1_out[4]), .Cin(full_adder_4_cout), .Sum(Output[4]), .Cout(full_adder_5_cout));
  Full_Adder full_adder_6 (
    .Data1(Data1[5]), .Data2(not_1_out[5]), .Cin(full_adder_5_cout), .Sum(Output[5]), .Cout(full_adder_6_cout));
  Full_Adder full_adder_7 (
    .Data1(Data1[6]), .Data2(not_1_out[6]), .Cin(full_adder_6_cout), .Sum(Output[6]), .Cout(full_adder_7_cout));
  Full_Adder full_adder_8 (
    .Data1(Data1[7]), .Data2(not_1_out[7]), .Cin(full_adder_7_cout), .Sum(Output[7]), .Cout(full_adder_8_cout));
  Full_Adder full_adder_9 (
    .Data1(Data1[8]), .Data2(not_1_out[8]), .Cin(full_adder_8_cout), .Sum(Output[8]), .Cout(full_adder_9_cout));
  Full_Adder full_adder_10 (
    .Data1(Data1[9]), .Data2(not_1_out[9]), .Cin(full_adder_9_cout), .Sum(Output[9]),
    .Cout(full_adder_10_cout));
  Full_Adder full_adder_11 (
    .Data1(Data1[10]), .Data2(not_1_out[10]), .Cin(full_adder_10_cout), .Sum(Output[10]),
    .Cout(full_adder_11_cout));
  Full_Adder full_adder_12 (
    .Data1(Data1[11]), .Data2(not_1_out[11]), .Cin(full_adder_11_cout), .Sum(Output[11]),
    .Cout(full_adder_12_cout));
  Full_Adder full_adder_13 (
    .Data1(Data1[12]), .Data2(not_1_out[12]), .Cin(full_adder_12_cout), .Sum(Output[12]),
    .Cout(full_adder_13_cout));
  Full_Adder full_adder_14 (
    .Data1(Data1[13]), .Data2(not_1_out[13]), .Cin(full_adder_13_cout), .Sum(Output[13]),
    .Cout(full_adder_14_cout));
  Full_Adder full_adder_15 (
    .Data1(Data1[14]), .Data2(not_1_out[14]), .Cin(full_adder_14_cout), .Sum(Output[14]),
    .Cout(full_adder_15_cout));
  Full_Adder full_adder_16 (
    .Data1(Data1[15]), .Data2(not_1_out[15]), .Cin(full_adder_15_cout), .Sum(Output[15]),
    .Cout(full_adder_16_cout));
  Full_Adder full_adder_17 (
    .Data1(Data1[16]), .Data2(not_1_out[16]), .Cin(full_adder_16_cout), .Sum(Output[16]),
    .Cout(full_adder_17_cout));
  Full_Adder full_adder_18 (
    .Data1(Data1[17]), .Data2(not_1_out[17]), .Cin(full_adder_17_cout), .Sum(Output[17]),
    .Cout(full_adder_18_cout));
  Full_Adder full_adder_19 (
    .Data1(Data1[18]), .Data2(not_1_out[18]), .Cin(full_adder_18_cout), .Sum(Output[18]),
    .Cout(full_adder_19_cout));
  Full_Adder full_adder_20 (
    .Data1(Data1[19]), .Data2(not_1_out[19]), .Cin(full_adder_19_cout), .Sum(Output[19]),
    .Cout(full_adder_20_cout));
  Full_Adder full_adder_21 (
    .Data1(Data1[20]), .Data2(not_1_out[20]), .Cin(full_adder_20_cout), .Sum(Output[20]),
    .Cout(full_adder_21_cout));
  Full_Adder full_adder_22 (
    .Data1(Data1[21]), .Data2(not_1_out[21]), .Cin(full_adder_21_cout), .Sum(Output[21]),
    .Cout(full_adder_22_cout));
  Full_Adder full_adder_23 (
    .Data1(Data1[22]), .Data2(not_1_out[22]), .Cin(full_adder_22_cout), .Sum(Output[22]),
    .Cout(full_adder_23_cout));
  Full_Adder full_adder_24 (
    .Data1(Data1[23]), .Data2(not_1_out[23]), .Cin(full_adder_23_cout), .Sum(Output[23]),
    .Cout(full_adder_24_cout));
  Full_Adder full_adder_25 (
    .Data1(Data1[24]), .Data2(not_1_out[24]), .Cin(full_adder_24_cout), .Sum(Output[24]),
    .Cout(full_adder_25_cout));
  Full_Adder full_adder_26 (
    .Data1(Data1[25]), .Data2(not_1_out[25]), .Cin(full_adder_25_cout), .Sum(Output[25]),
    .Cout(full_adder_26_cout));
  Full_Adder full_adder_27 (
    .Data1(Data1[26]), .Data2(not_1_out[26]), .Cin(full_adder_26_cout), .Sum(Output[26]),
    .Cout(full_adder_27_cout));
  Full_Adder full_adder_28 (
    .Data1(Data1[27]), .Data2(not_1_out[27]), .Cin(full_adder_27_cout), .Sum(Output[27]),
    .Cout(full_adder_28_cout));
  Full_Adder full_adder_29 (
    .Data1(Data1[28]), .Data2(not_1_out[28]), .Cin(full_adder_28_cout), .Sum(Output[28]),
    .Cout(full_adder_29_cout));
  Full_Adder full_adder_30 (
    .Data1(Data1[29]), .Data2(not_1_out[29]), .Cin(full_adder_29_cout), .Sum(Output[29]),
    .Cout(full_adder_30_cout));
  Full_Adder full_adder_31 (
    .Data1(Data1[30]), .Data2(not_1_out[30]), .Cin(full_adder_30_cout), .Sum(Output[30]),
    .Cout(full_adder_31_cout));
  Full_Adder full_adder_32 (
    .Data1(Data1[31]), .Data2(not_1_out[31]), .Cin(full_adder_31_cout), .Sum(Output[31]), .Cout(Overflow));
endmodule
